# Fritzing sketch Projeto_O2 (saved by Fritzing 0.8.7b)
breadboards: 1

parts:
  MÓDULO_IIC2 = LCM1602 IIC [part_number="LCM1602 IIC" chip_label="LCM1602 IIC" package="DIP (Dual Inline) [THT]"]
  Encoder_HW-040 = KY-040 Rotary encoder [package=THT]
  LCD2004-I2C1 = LCD2004-I2C  # not connected
  Motor_de_Passo_NEMA23 = Stepper Motor - Bipolar
  Arduino_Uno_R3 = Arduino Uno (Rev3) - ICSP
  TB6600_Microstep_Driver = TB6600 Microstep driver [part_number="Adafruit #2448"]
  Bateria_12V_2A = Battery block 12V
  Sensor_Indutivo_LJ12A3-4_ZBX = LJ12A3-4-Z [package=THT]
  M4 = LJ12A3-4-Z [package=THT]
  J7 = Screw terminal - 2 pins [package=THT]  # not connected
  OPTOACOPLADOR_TLP281-4 = TLP281-4 [package=THT]
  Módulo_HC05 = Bluetooth HC-05 Macho
  R1 = Resistor [tolerance=±5% resistance=220 package=THT]
  R2 = Resistor [tolerance=±5% resistance=390 package=THT]

nets:
  GND: MÓDULO_IIC2.GND, Encoder_HW-040.GND, Arduino_Uno_R3.GND, TB6600_Microstep_Driver.GND, TB6600_Microstep_Driver.DIR-, TB6600_Microstep_Driver.PULL-, Bateria_12V_2A.-, Sensor_Indutivo_LJ12A3-4_ZBX.GND, M4.GND, OPTOACOPLADOR_TLP281-4.HVCC, OPTOACOPLADOR_TLP281-4.OUT4, Módulo_HC05.GND, R2.Pin_0
  VCC: MÓDULO_IIC2.VCC, Encoder_HW-040.Vcc, OPTOACOPLADOR_TLP281-4.HGND, Módulo_HC05.VCC
  N1: MÓDULO_IIC2.SDA, Arduino_Uno_R3.A4/SDA
  N2: MÓDULO_IIC2.SCL, Arduino_Uno_R3.A5/SCL
  N3: Encoder_HW-040.SW, Arduino_Uno_R3.A3
  N4: Encoder_HW-040.DT, Arduino_Uno_R3.A2
  N5: Encoder_HW-040.CLK, Arduino_Uno_R3.A1
  N6: Motor_de_Passo_NEMA23.A, TB6600_Microstep_Driver.B-
  N7: Motor_de_Passo_NEMA23.C, TB6600_Microstep_Driver.B+
  N8: Motor_de_Passo_NEMA23.B, TB6600_Microstep_Driver.A-
  N9: Motor_de_Passo_NEMA23.D, TB6600_Microstep_Driver.A+
  N10: Arduino_Uno_R3.D9_PWM, OPTOACOPLADOR_TLP281-4.OUT2
  N11: Arduino_Uno_R3.D10_PWM/SS, OPTOACOPLADOR_TLP281-4.OUT1
  N12: Arduino_Uno_R3.D11_PWM/MOSI, TB6600_Microstep_Driver.PULL+
  N13: Arduino_Uno_R3.D12/MISO, TB6600_Microstep_Driver.DIR+
  N14: Arduino_Uno_R3.D0/RX, Módulo_HC05.TXD
  N15: Arduino_Uno_R3.D1/TX, Módulo_HC05.RXD, R1.Pin_0, R1.Pin_1, R2.Pin_1
  VCC_2: TB6600_Microstep_Driver.VCC, Bateria_12V_2A.+, Sensor_Indutivo_LJ12A3-4_ZBX.VCC, M4.VCC
  N16: Sensor_Indutivo_LJ12A3-4_ZBX.CARGA, OPTOACOPLADOR_TLP281-4.IN1
  N17: M4.CARGA, OPTOACOPLADOR_TLP281-4.IN2

custom parts:
  LCM1602 IIC: I2C-Module to use a 1602 or 2004 LCD on with the wire.h libory Serial LCD Modul
  KY-040 Rotary encoder: KY-040 Rotary Encoder with switch on breakout borad from AZ Delivery
  LCD2004-I2C: A standard character display with 4x20 characters. Comes in many colors with LCM2004 IIC attached.
  TB6600 Microstep driver: Driver controlador para motor de passo tb6600
  Battery block 12V: Your standard 9 Volts battery block
  LJ12A3-4-Z: LJ12A3-4-Z Proximity Sensor module.220V normally open.
  TLP281-4: TLP281-4 Optocoupler - keeps you from frying your stuff!
